# Fritzing sketch project (saved by Fritzing 0.9.3b)
breadboards: 1

parts:
  Part1 = Arduino Uno (Rev3)
  DHT11_1 = DHT11 module
  U1 = ESP8266 WiFi Module [part_number=ESP8266]
  GSM_SIM_GPSR_SMS_SIM900_SIM1 = SIM800L [package=THT]
  R1 = Resistor [tolerance=±5% resistance=220 package=THT]
  R2 = Resistor [tolerance=±5% resistance=220 package=THT]
  R3 = Resistor [tolerance=±5% resistance=220 package=THT]
  R4 = Resistor [tolerance=±5% resistance=220 package=THT]

nets:
  N1: Part1.D12/MISO, DHT11_1.DATA
  N2: Part1.D2, R2.Pin_1
  N3: Part1.D3_PWM, R1.Pin_0
  N4: Part1.D4, GSM_SIM_GPSR_SMS_SIM900_SIM1.SIM_TXD
  N5: Part1.D5_PWM, GSM_SIM_GPSR_SMS_SIM900_SIM1.SIM_RXD
  3V3: Part1.3V3, U1.VCC
  5V: Part1.5V, DHT11_1.VCC, GSM_SIM_GPSR_SMS_SIM900_SIM1.5V
  GND: Part1.GND, DHT11_1.GND, U1.GND, GSM_SIM_GPSR_SMS_SIM900_SIM1.GND, R3.Pin_1, R4.Pin_1
  N6: U1.RXD, R1.Pin_1, R3.Pin_0
  N7: U1.TXD, R2.Pin_0, R4.Pin_0

custom parts:
  DHT11 module: DHT11 black pcb module
  ESP8266 WiFi Module: Generic WiFi Module based on the ESP8266 with onboard PCB antenna and UART communications
